// Logisim project lab3.circ as structural Verilog: 7 circuits, main circuit Main
module Main (
);

  wire ALUSrcA, and_1_out, Clock, ifBranch, IorD, IRWrite, JAL, jr, MemRead, MemtoReg, MemWrite, or_1_out,
       PCWrite, RegDest, RegWrite, Zero;
  wire [1:0] ALUSrcB, PCSource;
  wire [3:0] ALUCtrl, ALUOp, CurrentState, NextState;
  wire [4:0] multiplexer_3_out;
  wire [5:0] _0_5, _26_31;
  wire [7:0] multiplexer_1_out;
  wire [15:6] _0_15;
  wire [25:16] _0_25;
  wire [27:0] shifter_2_out;
  wire [31:0] A_q, alu_1_aluresult, ALUout, B, B_q, bit_extender_1_out, IR, MDRR, multiplexer_2_out,
       multiplexer_4_out, multiplexer_5_out, PC, PCout, register_file_1_rddata1, register_file_1_rddata2,
       shifter_1_out;

  Clock clock_1 (.out(Clock));
  or or_1 (or_1_out, PCWrite, and_1_out);
  Register #(.width(32)) register_1 (.D(PCout), .en(or_1_out), .Q(PC), .clk(Clock));  // open: clr
  and and_1 (and_1_out, ifBranch, Zero);
  // Probe on CurrentState
  // Probe on NextState
  // Probe on PC
  // Probe on ALUout
  Multiplexer #(.width(8)) multiplexer_1 (
    .in0(PC[9:2]), .in1(ALUout[7:0]), .out(multiplexer_1_out), .sel(IorD));  // open: en
  // Probe on multiplexer_1_out
  // Probe on B
  // Probe on IR
  // Probe on IR
  RAM #(.dataWidth(32), .bus("separate")) ram_1 (
    .addr(multiplexer_1_out), .din(B), .data(IR), .str(MemWrite), .clk(Clock), .ld(MemRead));  // open: sel, clr
  // Probe on CurrentState
  // Probe on NextState
  // Probe on {_26_31, _0_25, _0_15, _0_5}
  Register #(.width(32)) u_IR (.D(IR), .en(IRWrite), .Q({_26_31, _0_25, _0_15, _0_5}), .clk(Clock));  // open: clr
  // Probe on IR
  // Probe on MDRR
  Register #(.width(32)) MDR (.D(IR), .Q(MDRR), .clk(Clock));  // open: en, clr
  Multiplexer #(.width(32)) multiplexer_2 (
    .in0(ALUout), .in1(IR), .out(multiplexer_2_out), .sel(MemtoReg));  // open: en
  // Probe on multiplexer_2_out
  // Probe on _26_31
  Multiplexer #(.width(5)) multiplexer_3 (
    .in0(_0_15[15:11]), .in1(_0_25[20:16]), .out(multiplexer_3_out), .sel(RegDest));  // open: en
  Control_Unit Control_Unit (
    .Opcode(_26_31), .Clock(Clock), .Jal(JAL), .jr(jr), .PCSource(PCSource), .AluOp(ALUOp),
    .ALUSrcB(ALUSrcB), .ALUSrcA(ALUSrcA), .RegWrite(RegWrite), .RegDst(RegDest), .IRWrite(IRWrite),
    .MemtoReg(MemtoReg), .MemWrite(MemWrite), .MemRead(MemRead), .IorD(IorD), .PCWrite(PCWrite),
    .ifBranch(ifBranch), .CurrentState(CurrentState), .NextState(NextState));
  // Probe on multiplexer_3_out
  // Probe on _0_25[20:16]
  // Probe on _0_25[25:21]
  // Probe on PCSource
  // Probe on ALUOp
  // Probe on ALUSrcB
  // Probe on register_file_1_rddata1
  Register_File register_file_1 (
    .WrAddr(multiplexer_3_out), .WrData(multiplexer_2_out), .WrReg(RegWrite), .RdAddr1(_0_25[25:21]),
    .RdAddr2(_0_25[20:16]), .RdData1(register_file_1_rddata1), .RdData2(register_file_1_rddata2),
    .Clock(Clock));
  // Probe on register_file_1_rddata2
  Register #(.width(32)) A (.D(register_file_1_rddata1), .Q(A_q), .clk(Clock));  // open: en, clr
  Register #(.width(32)) u_B (.D(register_file_1_rddata2), .Q(B_q), .clk(Clock));  // open: en, clr
  assign bit_extender_1_out = {{16{_0_15[15]}}, {_0_15, _0_5}};  // Bit_Extender bit_extender_1
  Shifter #(.width(32)) shifter_1 (.in(bit_extender_1_out), .\dist (5'b00010), .out(shifter_1_out));
  // Probe on ALUSrcB
  ALUCtrl u_ALUCtrl (
    .Op3(ALUOp[3]), .Op2(ALUOp[2]), .Op1(ALUOp[1]), .Op0(ALUOp[0]), .Func5(_0_5[5]), .Func4(_0_5[4]),
    .Func3(_0_5[3]), .Func2(_0_5[2]), .Func1(_0_5[1]), .Func0(_0_5[0]), .ALUCtrl3(ALUCtrl[3]),
    .ALUCtrl2(ALUCtrl[2]), .ALUCtrl1(ALUCtrl[1]), .ALUCtrl0(ALUCtrl[0]));
  Multiplexer #(.width(32)) multiplexer_4 (.in0(PC), .in1(A_q), .out(multiplexer_4_out), .sel(ALUSrcA));  // open: en
  Multiplexer #(.select(2), .width(32)) multiplexer_5 (
    .in0(B_q), .in1(32'h4), .in2(bit_extender_1_out), .in3(shifter_1_out), .out(multiplexer_5_out),
    .sel(ALUSrcB));  // open: en
  // Probe on multiplexer_4_out
  // Probe on multiplexer_5_out
  // Probe on ALUCtrl
  ALU alu_1 (
    .ALUCtl(ALUCtrl), .A(multiplexer_4_out), .B(multiplexer_5_out), .ALUResult(alu_1_aluresult), .Zero(Zero),
    .Shamt(_0_15[10:6]));  // open: Overflow
  Shifter #(.width(28)) shifter_2 (.in({_0_25, _0_15, _0_5, 2'b00}), .\dist (5'b00010), .out(shifter_2_out));
  Register #(.width(32)) A_2 (.D(alu_1_aluresult), .Q(ALUout), .clk(Clock));  // open: en, clr
  // Probe on ALUout
  // Probe on PCSource
  Multiplexer #(.select(2), .width(32)) multiplexer_6 (
    .in0(alu_1_aluresult), .in1(ALUout), .in2({PC[31:28], shifter_2_out}), .out(PCout), .sel(PCSource));  // open: in3, en
  // Probe on PCout
  // Probe on nothing
  // Probe on nothing
  // Probe on nothing
  // Probe on nothing
  // Probe on nothing
  // Probe on nothing
  // Probe on nothing
  // Probe on nothing
  // Probe on nothing
  // Probe on nothing

  // Other names for the same wires on the sheet: _0_15[5:0] = _0_5; _0_25[15:0] = {_0_15, _0_5};
  //   _6_10[4:0] = _0_15[10:6]; _11_15[4:0] = _0_15[15:11]; _16_20[4:0] = _0_25[20:16]; _21_25[4:0] = _0_25[25:21];
  //   MDR[31:0] = IR
endmodule

module _32_Bit_Adder___Subtractor (
  input  Add_Sub_control,
  input  [31:0] in_2,
  input  [31:0] in_3,
  output [31:0] out_4,
  output carry_out
);

  wire adder_1_cout, subtractor_1_bout;
  wire [31:0] adder_1_out, subtractor_1_out;

  Adder #(.width(32)) adder_1 (.a(in_2), .b(in_3), .out(adder_1_out), .cout(adder_1_cout));  // open: cin
  Subtractor #(.width(32)) subtractor_1 (
    .a(in_2), .b(in_3), .out(subtractor_1_out), .bout(subtractor_1_bout));  // open: bin
  Multiplexer #(.width(32), .enable("false")) multiplexer_1 (
    .in0(adder_1_out), .in1(subtractor_1_out), .out(out_4), .sel(Add_Sub_control));
  Multiplexer #(.enable("false")) multiplexer_2 (
    .in0(adder_1_cout), .in1(subtractor_1_bout), .out(carry_out), .sel(Add_Sub_control));
endmodule

module ALU (
  input  [3:0] ALUCtl,
  input  [31:0] A,
  input  [31:0] B,
  input  [4:0] Shamt,
  output [31:0] ALUResult,
  output Zero,
  output Overflow
);

  wire comparator_1_lt, comparator_2_lt, comparator_3_eq, comparator_4_eq, or_2_out;
  wire [31:0] Add, And, LessThan, LessThanUnsigned, Nor, Or, ShiftLeft, ShiftRight, Sub, Xor;

  // Probe on ALUCtl
  assign Nor = ~(A | B);  // NOR_Gate nor_1, 32 bits wide
  Adder #(.width(32)) adder_1 (.a(A), .b(B), .out(Add));  // open: cin, cout
  Subtractor #(.width(32)) subtractor_1 (.a(A), .b(B), .out(Sub));  // open: bin, bout
  assign And = A & B;  // AND_Gate and_1, 32 bits wide
  assign Or = A | B;  // OR_Gate or_1, 32 bits wide
  assign Xor = A ^ B;  // XOR_Gate xor_1, 32 bits wide
  Comparator #(.width(32)) comparator_1 (.a(A), .b(B), .lt(comparator_1_lt));  // open: gt, eq
  assign LessThan = {{31{1'b0}}, comparator_1_lt};  // Bit_Extender bit_extender_1
  Shifter #(.width(32)) shifter_1 (.in(B), .\dist (Shamt), .out(ShiftLeft));
  Shifter #(.width(32), .shift("lr")) shifter_2 (.in(B), .\dist (Shamt), .out(ShiftRight));
  Comparator #(.width(32), .mode("unsigned")) comparator_2 (.a(A), .b(B), .lt(comparator_2_lt));  // open: gt, eq
  assign LessThanUnsigned = {{31{1'b0}}, comparator_2_lt};  // Bit_Extender bit_extender_2
  Multiplexer #(.select(4), .width(32), .enable("false")) multiplexer_1 (
    .in0(Or), .in1(LessThanUnsigned), .in2(LessThan), .in3(Add), .in4(Sub), .in5(Xor), .in6(And),
    .in14(ShiftRight), .in15(ShiftLeft), .out(ALUResult), .sel(ALUCtl));  // open: in7, in8, in9, in10, in11, in12, in13
  Comparator #(.width(4)) comparator_3 (.a(4'b0011), .b(ALUCtl), .eq(comparator_3_eq));  // open: gt, lt
  Comparator #(.width(4)) comparator_4 (.a(ALUCtl), .b(4'b0100), .eq(comparator_4_eq));  // open: gt, lt
  Overflow overflow_1 (
    .Add(comparator_3_eq), .Sub(comparator_4_eq), .ASign(A[31]), .BSign(B[31]), .ResultSign(ALUResult[31]),
    .Overflow(Overflow));
  not not_1 (Zero, or_2_out);
  or or_2 (or_2_out, ALUResult[0], ALUResult[1], ALUResult[2], ALUResult[3], ALUResult[4], ALUResult[5], ALUResult[6], ALUResult[7], ALUResult[8], ALUResult[9], ALUResult[10], ALUResult[11], ALUResult[12], ALUResult[13], ALUResult[14], ALUResult[15], ALUResult[16], ALUResult[17], ALUResult[18], ALUResult[19], ALUResult[20], ALUResult[21], ALUResult[22], ALUResult[23], ALUResult[24], ALUResult[25], ALUResult[26], ALUResult[27], ALUResult[28], ALUResult[29], ALUResult[30], ALUResult[31]);

  // Other names for the same wires on the sheet: ASign = A[31]; ResultSign = ALUResult[31]; BSign = B[31]
endmodule

module Register_File (
  input  [4:0] WrAddr,
  input  [31:0] WrData,
  input  WrReg,
  input  [4:0] RdAddr1,
  input  [4:0] RdAddr2,
  input  Clock,
  output [31:0] RdData1,
  output [31:0] RdData2
);

  wire WrReg0, WrReg1, WrReg2, WrReg3, WrReg4, WrReg5, WrReg6, WrReg7, WrReg8, WrReg9, WrReg10, WrReg11,
       WrReg12, WrReg13, WrReg14, WrReg15, WrReg16, WrReg17, WrReg18, WrReg19, WrReg20, WrReg21, WrReg22,
       WrReg23, WrReg24, WrReg25, WrReg26, WrReg27, WrReg28, WrReg29, WrReg30, WrReg31;
  wire [31:0] RegData1, RegData2, RegData3, RegData4, RegData5, RegData6, RegData7, RegData8, RegData9,
       RegData10, RegData11, RegData12, RegData13, RegData14, RegData15, RegData16, RegData17, RegData18,
       RegData19, RegData20, RegData21, RegData22, RegData23, RegData24, RegData25, RegData26, RegData27,
       RegData28, RegData29, RegData30, RegData31;

  Demultiplexer #(.select(5), .enable("false")) demultiplexer_1 (
    .out0(WrReg0), .out1(WrReg1), .out2(WrReg2), .out3(WrReg3), .out4(WrReg4), .out5(WrReg5), .out6(WrReg6),
    .out7(WrReg7), .out8(WrReg8), .out9(WrReg9), .out10(WrReg10), .out11(WrReg11), .out12(WrReg12),
    .out13(WrReg13), .out14(WrReg14), .out15(WrReg15), .out16(WrReg16), .out17(WrReg17), .out18(WrReg18),
    .out19(WrReg19), .out20(WrReg20), .out21(WrReg21), .out22(WrReg22), .out23(WrReg23), .out24(WrReg24),
    .out25(WrReg25), .out26(WrReg26), .out27(WrReg27), .out28(WrReg28), .out29(WrReg29), .out30(WrReg30),
    .out31(WrReg31), .in(WrReg), .sel(WrAddr));
  // Probe on RegData4
  Register #(.width(32)) Reg4 (.D(WrData), .en(WrReg4), .Q(RegData4), .clk(Clock));  // open: clr
  // Probe on RegData8
  Register #(.width(32)) Reg8 (.D(WrData), .en(WrReg8), .Q(RegData8), .clk(Clock));  // open: clr
  // Probe on RegData12
  Register #(.width(32)) Reg12 (.D(WrData), .en(WrReg12), .Q(RegData12), .clk(Clock));  // open: clr
  // Probe on RegData16
  Register #(.width(32)) Reg16 (.D(WrData), .en(WrReg16), .Q(RegData16), .clk(Clock));  // open: clr
  // Probe on RegData20
  Register #(.width(32)) Reg20 (.D(WrData), .en(WrReg20), .Q(RegData20), .clk(Clock));  // open: clr
  // Probe on RegData24
  Register #(.width(32)) Reg24 (.D(WrData), .en(WrReg24), .Q(RegData24), .clk(Clock));  // open: clr
  // Probe on RegData28
  Register #(.width(32)) Reg28 (.D(WrData), .en(WrReg28), .Q(RegData28), .clk(Clock));  // open: clr
  Register #(.width(32)) Reg1 (.D(WrData), .en(WrReg1), .Q(RegData1), .clk(Clock));  // open: clr
  Register #(.width(32)) Reg5 (.D(WrData), .en(WrReg5), .Q(RegData5), .clk(Clock));  // open: clr
  Register #(.width(32)) Reg9 (.D(WrData), .en(WrReg9), .Q(RegData9), .clk(Clock));  // open: clr
  Register #(.width(32)) Reg13 (.D(WrData), .en(WrReg13), .Q(RegData13), .clk(Clock));  // open: clr
  Register #(.width(32)) Reg17 (.D(WrData), .en(WrReg17), .Q(RegData17), .clk(Clock));  // open: clr
  Register #(.width(32)) Reg21 (.D(WrData), .en(WrReg21), .Q(RegData21), .clk(Clock));  // open: clr
  Register #(.width(32)) Reg25 (.D(WrData), .en(WrReg25), .Q(RegData25), .clk(Clock));  // open: clr
  Register #(.width(32)) Reg29 (.D(WrData), .en(WrReg29), .Q(RegData29), .clk(Clock));  // open: clr
  // Probe on RegData1
  // Probe on RegData5
  // Probe on RegData9
  // Probe on RegData13
  // Probe on RegData17
  // Probe on RegData21
  // Probe on RegData25
  // Probe on RegData29
  // Probe on RegData2
  Register #(.width(32)) Reg2 (.D(WrData), .en(WrReg2), .Q(RegData2), .clk(Clock));  // open: clr
  // Probe on RegData6
  Register #(.width(32)) Reg6 (.D(WrData), .en(WrReg6), .Q(RegData6), .clk(Clock));  // open: clr
  // Probe on RegData10
  Register #(.width(32)) Reg10 (.D(WrData), .en(WrReg10), .Q(RegData10), .clk(Clock));  // open: clr
  // Probe on RegData14
  Register #(.width(32)) Reg14 (.D(WrData), .en(WrReg14), .Q(RegData14), .clk(Clock));  // open: clr
  // Probe on RegData18
  Register #(.width(32)) Reg18 (.D(WrData), .en(WrReg18), .Q(RegData18), .clk(Clock));  // open: clr
  // Probe on RegData22
  Register #(.width(32)) Reg22 (.D(WrData), .en(WrReg22), .Q(RegData22), .clk(Clock));  // open: clr
  // Probe on RegData26
  Register #(.width(32)) Reg26 (.D(WrData), .en(WrReg26), .Q(RegData26), .clk(Clock));  // open: clr
  // Probe on RegData30
  Register #(.width(32)) Reg30 (.D(WrData), .en(WrReg30), .Q(RegData30), .clk(Clock));  // open: clr
  // Probe on RegData3
  Register #(.width(32)) Reg3 (.D(WrData), .en(WrReg3), .Q(RegData3), .clk(Clock));  // open: clr
  // Probe on RegData7
  Register #(.width(32)) Reg7 (.D(WrData), .en(WrReg7), .Q(RegData7), .clk(Clock));  // open: clr
  // Probe on RegData11
  Register #(.width(32)) Reg11 (.D(WrData), .en(WrReg11), .Q(RegData11), .clk(Clock));  // open: clr
  // Probe on RegData15
  Register #(.width(32)) Reg15 (.D(WrData), .en(WrReg15), .Q(RegData15), .clk(Clock));  // open: clr
  // Probe on RegData19
  Register #(.width(32)) Reg19 (.D(WrData), .en(WrReg19), .Q(RegData19), .clk(Clock));  // open: clr
  // Probe on RegData23
  Register #(.width(32)) Reg23 (.D(WrData), .en(WrReg23), .Q(RegData23), .clk(Clock));  // open: clr
  // Probe on RegData27
  Register #(.width(32)) Reg27 (.D(WrData), .en(WrReg27), .Q(RegData27), .clk(Clock));  // open: clr
  // Probe on RegData31
  Register #(.width(32)) Reg31 (.D(WrData), .en(WrReg31), .Q(RegData31), .clk(Clock));  // open: clr
  Multiplexer #(.select(5), .width(32), .enable("false")) multiplexer_1 (
    .in0({32{1'b0}}), .in1(RegData1), .in2(RegData2), .in3(RegData3), .in4(RegData4), .in5(RegData5),
    .in6(RegData6), .in7(RegData7), .in8(RegData8), .in9(RegData9), .in10(RegData10), .in11(RegData11),
    .in12(RegData12), .in13(RegData13), .in14(RegData14), .in15(RegData15), .in16(RegData16),
    .in17(RegData17), .in18(RegData18), .in19(RegData19), .in20(RegData20), .in21(RegData21),
    .in22(RegData22), .in23(RegData23), .in24(RegData24), .in25(RegData25), .in26(RegData26),
    .in27(RegData27), .in28(RegData28), .in29(RegData29), .in30(RegData30), .in31(RegData31), .out(RdData1),
    .sel(RdAddr1));
  Multiplexer #(.select(5), .width(32), .enable("false")) multiplexer_2 (
    .in0({32{1'b0}}), .in1(RegData1), .in2(RegData2), .in3(RegData3), .in4(RegData4), .in5(RegData5),
    .in6(RegData6), .in7(RegData7), .in8(RegData8), .in9(RegData9), .in10(RegData10), .in11(RegData11),
    .in12(RegData12), .in13(RegData13), .in14(RegData14), .in15(RegData15), .in16(RegData16),
    .in17(RegData17), .in18(RegData18), .in19(RegData19), .in20(RegData20), .in21(RegData21),
    .in22(RegData22), .in23(RegData23), .in24(RegData24), .in25(RegData25), .in26(RegData26),
    .in27(RegData27), .in28(RegData28), .in29(RegData29), .in30(RegData30), .in31(RegData31), .out(RdData2),
    .sel(RdAddr2));
endmodule

module Overflow (
  input  Add,
  input  Sub,
  input  ASign,
  input  BSign,
  input  ResultSign,
  output Overflow
);

  wire and_1_out, and_2_out, or_1_out, xnor_1_out, xor_1_out, xor_2_out;

  xnor xnor_1 (xnor_1_out, ASign, BSign);
  xor xor_1 (xor_1_out, ASign, BSign);
  and and_1 (and_1_out, xnor_1_out, Add);
  and and_2 (and_2_out, xor_1_out, Sub);
  or or_1 (or_1_out, and_1_out, and_2_out);
  xor xor_2 (xor_2_out, ResultSign, ASign);
  and and_3 (Overflow, or_1_out, xor_2_out);

  // Notes on the sheet:
  //   Overflow occurs when doing addition and sign(A) == sign(B) && sign(result) != sign(A)
  //   Or
  //   Overflow occurs when doing subtraction and sign(A) != sign(B) && sign(result) != sign(A)
endmodule

module Control_Unit (
  input  [5:0] Opcode,
  input  Clock,
  output Jal,
  output jr,
  output [1:0] PCSource,
  output [3:0] AluOp,
  output [1:0] ALUSrcB,
  output ALUSrcA,
  output RegWrite,
  output RegDst,
  output IRWrite,
  output MemtoReg,
  output MemWrite,
  output MemRead,
  output IorD,
  output PCWrite,
  output ifBranch,
  output [3:0] CurrentState,
  output [3:0] NextState
);

  // Probe on NextState
  Register #(.width(4)) register_1 (.D(NextState), .Q(CurrentState), .clk(Clock));  // open: en, clr
  // Probe on CurrentState
  ROM #(.addrWidth(10), .dataWidth(24)) rom_1 (
    .addr({Opcode, CurrentState}),
    .data({Jal, jr, NextState, PCSource, AluOp, ALUSrcB, ALUSrcA, RegWrite, RegDst, IRWrite, MemtoReg, MemWrite, MemRead, IorD, PCWrite, ifBranch}));  // open: sel
  // Probe on {Jal, jr, NextState, PCSource, AluOp, ALUSrcB, ALUSrcA, RegWrite, RegDst, IRWrite, MemtoReg, MemWrite, MemRead, IorD, PCWrite, ifBranch}
  // Probe on NextState

  // Notes on the sheet:
  //   contents of rom_1 (hex, n*v repeats v):
  //   4344a 180c00 3a00 10000c 180 14 1c8200 180 240a00 180 4201 2 800002 400002 0 0 4344a c00 3a00 10000c
  //   180 14 1c8200 180 240a00 180 4201 2 800002 400002 0 0 4344a 2c0c00 3a00 10000c 180 14 1c8200 180
  //   240a00 180 4201 2 800002 400002 0 0 4344a 300c00 3a00 10000c 180 14 1c8200 180 240a00 180 4201 2
  //   800002 400002 0 0 4344a 280c00 3a00 10000c 180 14 1c8200 180 240a00 180 4201 2 800002 400002 0 0
  //   4344a c00 3a00 10000c 180 14 1c8200 180 240a00 180 4201 2 800002 400002 0 0 4344a c00 3a00 10000c
  //   180 14 1c8200 180 240a00 180 4201 2 800002 400002 0 0 4344a c00 3a00 10000c 180 14 1c8200 180 240a00
  //   180 4201 2 800002 400002 0 0 4344a 200c00 3a00 10000c 180 14 1c8200 180 240a00 180 4201 2 800002
  //   400002 0 0 4344a c00 3a00 10000c 180 14 1c8200 180 240a00 180 4201 2 800002 400002 0 0 4344a c00
  //   3a00 10000c 180 14 1c8200 180 240a00 180 4201 2 800002 400002 0 0 4344a c00 3a00 10000c 180 14
  //   1c8200 180 240a00 180 4201 2 800002 400002 0 0 4344a 200c00 3a00 10000c 180 14 1c8200 180 240a00 180
  //   4201 2 800002 400002 0 0 4344a 200c00 3a00 10000c 180 14 1c8200 180 240a00 180 4201 2 800002 400002
  //   0 0 4344a c00 3a00 10000c 180 14 1c8200 180 240a00 180 4201 2 800002 400002 0 0 4344a c00 3a00
  //   10000c 180 14 1c8200 180 240a00 180 4201 2 800002 400002 0 0 4344a c00 3a00 10000c 180 14 1c8200 180
  //   240a00 180 4201 2 800002 400002 0 0 4344a c00 3a00 10000c 180 14 1c8200 180 240a00 180 4201 2 800002
  //   400002 0 0 4344a c00 3a00 10000c 180 14 1c8200 180 240a00 180 4201 2 800002 400002 0 0 4344a c00
  //   3a00 10000c 180 14 1c8200 180 240a00 180 4201 2 800002 400002 0 0 4344a c00 3a00 10000c 180 14
  //   1c8200 180 240a00 180 4201 2 800002 400002 0 0 4344a c00 3a00 10000c 180 14 1c8200 180 240a00 180
  //   4201 2 800002 400002 0 0 4344a c00 3a00 10000c 180 14 1c8200 180 240a00 180 4201 2 800002 400002 0 0
  //   4344a c00 3a00 10000c 180 14 1c8200 180 240a00 180 4201 2 800002 400002 0 0 4344a c00 3a00 10000c
  //   180 14 1c8200 180 240a00 180 4201 2 800002 400002 0 0 4344a c00 3a00 10000c 180 14 1c8200 180 240a00
  //   180 4201 2 800002 400002 0 0 4344a c00 3a00 10000c 180 14 1c8200 180 240a00 180 4201 2 800002 400002
  //   0 0 4344a c00 3a00 10000c 180 14 1c8200 180 240a00 180 4201 2 800002 400002 0 0 4344a c00 3a00
  //   10000c 180 14 1c8200 180 240a00 180 4201 2 800002 400002 0 0 4344a c00 3a00 10000c 180 14 1c8200 180
  //   240a00 180 4201 2 800002 400002 0 0 4344a c00 3a00 10000c 180 14 1c8200 180 240a00 180 4201 2 800002
  //   400002 0 0 4344a c00 3a00 10000c 180 14 1c8200 180 240a00 180 4201 2 800002 400002 0 0 4344a c00
  //   3a00 10000c 180 14 1c8200 180 240a00 180 4201 2 800002 400002 0 0 4344a c00 3a00 10000c 180 14
  //   1c8200 180 240a00 180 4201 2 800002 400002 0 0 4344a c00 3a00 10000c 180 14 1c8200 180 240a00 180
  //   4201 2 800002 400002 0 0 4344a 80c00 c3a00 10000c 180 14 1c8200 180 240a00 180 4201 2 800002 400002
  //   0 0 4344a c00 3a00 10000c 180 14 1c8200 180 240a00 180 4201 2 800002 400002 0 0 4344a c00 3a00
  //   10000c 180 14 1c8200 180 240a00 180 4201 2 800002 400002 0 0 4344a c00 3a00 10000c 180 14 1c8200 180
  //   240a00 180 4201 2 800002 400002 0 0 4344a c00 3a00 10000c 180 14 1c8200 180 240a00 180 4201 2 800002
  //   400002 0 0 4344a c00 3a00 10000c 180 14 1c8200 180 240a00 180 4201 2 800002 400002 0 0 4344a c00
  //   3a00 10000c 180 14 1c8200 180 240a00 180 4201 2 800002 400002 0 0 4344a c00 3a00 10000c 180 14
  //   1c8200 180 240a00 180 4201 2 800002 400002 0 0 4344a 80c00 143a00 10000c 180 14 1c8200 180 240a00
  //   180 4201 2 800002 400002 0 0 4344a c00 3a00 10000c 180 14 1c8200 180 240a00 180 4201 2 800002 400002
  //   0 0 4344a c00 3a00 10000c 180 14 1c8200 180 240a00 180 4201 2 800002 400002 0 0 4344a c00 3a00
  //   10000c 180 14 1c8200 180 240a00 180 4201 2 800002 400002 0 0 4344a c00 3a00 10000c 180 14 1c8200 180
  //   240a00 180 4201 2 800002 400002 0 0 4344a c00 3a00 10000c 180 14 1c8200 180 240a00 180 4201 2 800002
  //   400002 0 0 4344a c00 3a00 10000c 180 14 1c8200 180 240a00 180 4201 2 800002 400002 0 0 4344a c00
  //   3a00 10000c 180 14 1c8200 180 240a00 180 4201 2 800002 400002 0 0 4344a c00 3a00 10000c 180 14
  //   1c8200 180 240a00 180 4201 2 800002 400002 0 0 4344a c00 3a00 10000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
endmodule

module ALUCtrl (
  input  Op3,
  input  Op2,
  input  Op1,
  input  Op0,
  input  Func5,
  input  Func4,
  input  Func3,
  input  Func2,
  input  Func1,
  input  Func0,
  output ALUCtrl3,
  output ALUCtrl2,
  output ALUCtrl1,
  output ALUCtrl0
);

  wire and_1_out, and_2_out, and_3_out, and_4_out, and_5_out, and_6_out, and_7_out, and_8_out, and_9_out,
       and_10_out, and_11_out, and_12_out, not_1_out, not_2_out, not_3_out, not_4_out, not_5_out, not_6_out,
       not_7_out, not_8_out, not_9_out, not_10_out, not_11_out, not_12_out, not_13_out, not_14_out,
       not_15_out;

  not not_1 (not_1_out, Func5);
  not not_2 (not_2_out, Func5);
  not not_3 (not_3_out, Func3);
  not not_4 (not_4_out, Func2);
  not not_5 (not_5_out, Func3);
  not not_6 (not_6_out, Func5);
  not not_7 (not_7_out, Func2);
  not not_8 (not_8_out, Func1);
  not not_9 (not_9_out, Func0);
  not not_10 (not_10_out, Op2);
  not not_11 (not_11_out, Func1);
  not not_12 (not_12_out, Func0);
  not not_13 (not_13_out, Op2);
  not not_14 (not_14_out, Op2);
  not not_15 (not_15_out, Func0);
  and and_1 (and_1_out, Op2, Op1, Op0);
  and and_2 (and_2_out, Op3, not_1_out);
  and and_3 (and_3_out, Op3, Op1);
  and and_4 (and_4_out, Op3, not_2_out);
  and and_5 (and_5_out, Op3, not_3_out, not_4_out, Func0);
  and and_6 (and_6_out, Op3, not_5_out, Func1);
  and and_7 (and_7_out, Op3, not_6_out);
  and and_8 (and_8_out, Op3, not_7_out, not_8_out);
  and and_9 (and_9_out, Op3, Func3, not_9_out);
  and and_10 (and_10_out, Op3, not_10_out, not_11_out, not_12_out);
  and and_11 (and_11_out, Op3, not_13_out, Func1, Func0);
  and and_12 (and_12_out, Op3, not_14_out, Func2, not_15_out);
  or or_1 (ALUCtrl3, and_1_out, and_2_out, and_3_out);
  or or_2 (ALUCtrl2, Op2, and_4_out, and_5_out, and_6_out);
  or or_3 (ALUCtrl1, Op1, and_7_out, and_8_out, and_9_out);
  or or_4 (ALUCtrl0, Op0, and_10_out, and_11_out, and_12_out);
endmodule
